# Fritzing sketch klappe (saved by Fritzing 0.9.3b)
circuit board: 8.46667cm x 5.64444cm
breadboards: 1

parts:
  Part1 = Arduino Nano (Rev3.0)
  S1 = H-Bridge with L298N
  R1 = PHOTOCELL [package=photocell]
  M1 = DC Motor
  S2 = Momentary Switch [package=ksa_sealed_tac_switch]
  S3 = Momentary Switch [package=ksa_sealed_tac_switch]
  S4 = Momentary Switch [package=ksa_sealed_tac_switch]
  S5 = Momentary Switch [package=ksa_sealed_tac_switch]
  S8 = SWITCH-MOMENTARY-2 [package=reed_switch_plastic]
  S9 = SWITCH-MOMENTARY-2 [package=reed_switch_plastic]
  R2 = Resistor [tolerance=±5% resistance=220 package="0805 [SMD]"]
  Part2 = OLED Monochrome 128x32 I2C [part_number=931]
  ZS-042_RTC1 = ZS-042 RTC Module

nets:
  GND: Part1.GND, S1.GND, S2.3, S2.4, S3.3, S3.4, S4.3, S4.4, S5.3, S5.4, S8.2, S9.1, R2.Pin_0, Part2.GND, ZS-042_RTC1.GND
  N1: Part1.D2, S1.IN1
  N2: Part1.D3, S1.IN2
  N3: Part1.D4, S2.1, S2.2
  N4: Part1.D5, S3.1, S3.2
  N5: Part1.D6, S9.2
  N6: Part1.D7, S8.1
  N7: Part1.D8, S4.1, S4.2
  N8: Part1.D9, S5.1, S5.2
  5V: Part1.5V, S1.12V, R1.P$1, ZS-042_RTC1.VCC
  N9: Part1.A5, ZS-042_RTC1.SCL#3
  N10: Part1.A4, ZS-042_RTC1.SDA#2
  N11: Part1.A0, R1.P$2, R2.Pin_1
  3V3: Part1.3V3, Part2.3.3V
  N12: S1.M1-01, M1.pin_2
  N13: S1.M1-02, M1.pin_1
  N14: Part2.SCL, ZS-042_RTC1.SCL#9
  N15: Part2.SDA, ZS-042_RTC1.SDA#8

custom parts:
  H-Bridge with L298N: h-bridge
  OLED Monochrome 128x32 I2C: These displays are small, only about 1" diagonal, but very readable due to the high contrast of an OLED display. This display is made of 128x32 individual white OLED pixels, each one is turned on or off by the controller chip. Because the display makes its own light, no backlight is required. This reduces the power required to run the OLED and is why the display has such high contrast; we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
